// Logisim project SimpleTon_Design.circ as structural Verilog: 2 circuits, main circuit main
module main (
  input  ptCfR,
  input  pfCtR,
  input  [1:0] in_3,
  input  [7:0] in_4,
  input  in_5,
  input  EwtC
);

  wire decoder_1_out0, decoder_1_out1, decoder_1_out2, decoder_1_out3;
  wire [7:0] Core_q, doublesidedmultiplexer_1_lowero, doublesidedmultiplexer_1_uppero0,
       doublesidedmultiplexer_1_uppero1, doublesidedmultiplexer_1_uppero2, doublesidedmultiplexer_1_uppero3,
       multiplexer_1_out, R0_q, R1_q, R2_q, R3_q;

  Decoder #(.select(2)) decoder_1 (
    .out0(decoder_1_out0), .out1(decoder_1_out1), .out2(decoder_1_out2), .out3(decoder_1_out3), .sel(in_3));  // open: en
  Register #(.trigger("high")) R0 (
    .D(doublesidedmultiplexer_1_uppero0), .en(decoder_1_out0), .Q(R0_q), .clk(1'b1));  // open: clr
  Multiplexer #(.width(8), .enable("false")) multiplexer_1 (
    .in0(doublesidedmultiplexer_1_lowero), .in1(in_4), .out(multiplexer_1_out), .sel(in_5));
  Register #(.trigger("high")) R1 (
    .D(doublesidedmultiplexer_1_uppero1), .en(decoder_1_out1), .Q(R1_q), .clk(1'b1));  // open: clr
  Register #(.trigger("high")) Core (.D(multiplexer_1_out), .en(EwtC), .Q(Core_q), .clk(1'b1));  // open: clr
  Register #(.trigger("high")) R3 (
    .D(doublesidedmultiplexer_1_uppero3), .en(decoder_1_out3), .Q(R3_q), .clk(1'b1));  // open: clr
  Register #(.trigger("high")) R2 (
    .D(doublesidedmultiplexer_1_uppero2), .en(decoder_1_out2), .Q(R2_q), .clk(1'b1));  // open: clr
  DoubleSidedMultiplexer doublesidedmultiplexer_1 (
    .RSelect(in_3), .ptCfR(ptCfR), .pfCtR(pfCtR), .UpperI0(R0_q), .UpperO0(doublesidedmultiplexer_1_uppero0),
    .UpperI1(R1_q), .UpperO1(doublesidedmultiplexer_1_uppero1), .UpperI2(R2_q),
    .UpperO2(doublesidedmultiplexer_1_uppero2), .UpperI3(R3_q), .UpperO3(doublesidedmultiplexer_1_uppero3),
    .LowerO(doublesidedmultiplexer_1_lowero), .LowerI(Core_q));

  // Notes on the sheet:
  //   Keep in mind that the Output of a Register is the input for DSMUX and vice versa
  //   Issue: U need a multiplexer instead of an OR gate, which would require more work in the design
endmodule

// DSMUX
module DoubleSidedMultiplexer (
  input  [7:0] UpperI0,
  input  [7:0] UpperI1,
  input  [7:0] UpperI2,
  input  [7:0] UpperI3,
  input  [1:0] RSelect,
  input  ptCfR,
  input  pfCtR,
  input  [7:0] LowerI,
  output [7:0] UpperO0,
  output [7:0] UpperO1,
  output [7:0] UpperO2,
  output [7:0] UpperO3,
  output [7:0] LowerO
);

  Multiplexer #(.select(2), .width(8)) multiplexer_1 (
    .in0(UpperI0), .in1(UpperI1), .in2(UpperI2), .in3(UpperI3), .out(LowerO), .sel(RSelect), .en(ptCfR));
  Demultiplexer #(.select(2), .width(8)) demultiplexer_1 (
    .out0(UpperO0), .out1(UpperO1), .out2(UpperO2), .out3(UpperO3), .in(LowerI), .sel(RSelect), .en(pfCtR));
endmodule
